# Fritzing sketch phone-dialer (saved by Fritzing 0.8.5b)
breadboards: 1

parts:
  Part1 = Arduino Uno (Rev3)
  R1 = Resistor [tolerance=±5% resistance=100k package=THT]
  R2 = Resistor [tolerance=±5% resistance=100k package=THT]

nets:
  N1: Part1.D12/MISO, R1.Pin_0
  N2: Part1.D13/SCK, R2.Pin_0
  N3: Part1.GND, R1.Pin_1, R2.Pin_1
